# Fritzing sketch arduino4impress_schema (saved by Fritzing 0.7.1b)
breadboards: 1

parts:
  Arduino1 = Arduino
  R1 = Rotary Potentiometer (Small) [maximum_resistance=100kΩ]
  R2 = Resistor [tolerance=±5% resistance=560 package=THT]
  LED1 = LED - 5mm [color="Red (633nm)" package="5 mm [THT]"]
  LED2 = LED - 5mm [color="Red (633nm)" package="5 mm [THT]"]
  LED3 = LED - 5mm [color="Red (633nm)" package="5 mm [THT]"]
  LED4 = LED - 5mm [color="Red (633nm)" package="5 mm [THT]"]
  LED5 = LED - 5mm [color="Red (633nm)" package="5 mm [THT]"]
  R3 = Resistor [tolerance=±5% resistance=560 package=THT]
  R4 = Resistor [tolerance=±5% resistance=560 package=THT]
  R5 = Resistor [tolerance=±5% resistance=560 package=THT]
  R6 = Resistor [tolerance=±5% resistance=560 package=THT]

nets:
  N1: Arduino1.D12, LED1.anode
  N2: Arduino1.D11, LED2.anode
  N3: Arduino1.D10, LED3.anode
  N4: Arduino1.D9, LED4.anode
  N5: Arduino1.D8, LED5.anode
  N6: Arduino1.+5V, R1.leg1
  N7: Arduino1.GND, R1.leg2, R2.Pin_1, R3.Pin_1, R4.Pin_1, R5.Pin_1, R6.Pin_1
  N8: Arduino1.A0, R1.wiper
  N9: R2.Pin_0, LED1.cathode
  N10: LED2.cathode, R3.Pin_0
  N11: LED3.cathode, R4.Pin_0
  N12: LED4.cathode, R5.Pin_0
  N13: LED5.cathode, R6.Pin_0
